// Logisim project analyze.circ as structural Verilog: 1 circuit, main circuit main
module main (
  input  a,
  input  b,
  input  carry,
  output carry_out,
  output sum
);

  wire and_1_out, and_2_out, and_3_out, and_4_out, and_5_out, and_6_out, and_7_out, not_1_out, not_2_out,
       not_3_out, not_4_out, not_5_out, not_6_out;

  and and_1 (and_1_out, b, carry);
  and and_2 (and_2_out, a, carry);
  and and_3 (and_3_out, a, b);
  not not_1 (not_1_out, a);
  not not_2 (not_2_out, b);
  not not_3 (not_3_out, a);
  not not_4 (not_4_out, carry);
  not not_5 (not_5_out, b);
  not not_6 (not_6_out, carry);
  or or_1 (carry_out, and_1_out, and_2_out, and_3_out);
  and and_4 (and_4_out, not_1_out, not_2_out, carry);
  and and_5 (and_5_out, not_3_out, b, not_4_out);
  and and_6 (and_6_out, a, not_5_out, not_6_out);
  and and_7 (and_7_out, a, b, carry);
  or or_2 (sum, and_4_out, and_5_out, and_6_out, and_7_out);
endmodule
