// Logisim project attrlib_and_narrow.circ as structural Verilog: 1 circuit, main circuit main
module main (
  input  x,
  input  y,
  output x_XOR_y
);

  wire and_2_out, and_3_out, not_1_out, not_2_out;

  not not_1 (not_1_out, x);
  not not_2 (not_2_out, y);
  // AND_Gate and_1 is placed but not wired
  and and_2 (and_2_out, not_1_out, y);
  and and_3 (and_3_out, x, not_2_out);
  or or_1 (x_XOR_y, and_2_out, and_3_out);

  // Notes on the sheet:
  //   XOR
  //   Circuit construit avec
  //   Logisim-evolution
endmodule
