// Logisim project bundles_colors.circ as structural Verilog: 1 circuit, main circuit main
module main (
  input  in_1,
  input  in_2,
  input  in_3,
  input  [1:0] in_4,
  input  in_5,
  input  in_6,
  input  [1:0] in_7,
  input  in_8,
  input  in_9
);

  // Pins of 1 and 2 bits meet at in_7

  assign in_6 = in_5;
  assign in_8 = in_7[0];
endmodule
