// Logisim project bundles_index.circ as structural Verilog: 1 circuit, main circuit main
module main (
  input  [2:0] in_1,
  input  [2:0] in_2,
  input  in_3,
  input  in_4,
  output [2:0] out_5,
  output out_6
);

  assign out_5 = in_1 & in_2;  // AND_Gate and_1, 3 bits wide
  or or_1 (out_6, in_3, in_4);
endmodule
