// Logisim project bundles_splitter.circ as structural Verilog: 1 circuit, main circuit main
module main (
);


  // Notes on the sheet:
  //   Bus
  //   terminaison
  //   Gauche 
  //   Droite
  //   Centré
  //   Héritage
endmodule
