// Logisim project subcirc_2_done.circ as structural Verilog
module Mux_2To1 (
  input  In_0,
  input  In_1,
  input  Sel,
  output Out_1
);

  wire and_1_out, and_2_out, not_1_out;

  and and_1 (and_1_out, In_0, not_1_out);
  not not_1 (not_1_out, Sel);
  and and_2 (and_2_out, In_1, Sel);
  or or_1 (Out_1, and_1_out, and_2_out);
endmodule
