// Logisim project subcirc_4_add.circ as structural Verilog: 3 circuits, main circuit main
module main (
  input  In_0,
  input  IN_1,
  input  Sel,
  output Out_0
);

  wire and_1_out, and_2_out, not_1_out;

  not not_1 (not_1_out, Sel);
  and and_1 (and_1_out, In_0, not_1_out);
  and and_2 (and_2_out, IN_1, Sel);
  or or_1 (Out_0, and_1_out, and_2_out);
endmodule

module Mux_2To1 (
  input  In_0,
  input  In_1,
  input  Sel,
  output Out_1
);

  wire and_1_out, and_2_out, not_1_out;

  not not_1 (not_1_out, Sel);
  and and_1 (and_1_out, In_0, not_1_out);
  and and_2 (and_2_out, In_1, Sel);
  or or_1 (Out_1, and_1_out, and_2_out);
endmodule

module Mux_4To1 (
);

  Mux_2To1 mux_2to1_1 ();  // open: In_0, In_1, Sel, Out_1
  Mux_2To1 mux_2to1_2 ();  // open: In_0, In_1, Sel, Out_1
endmodule
