// Logisim project subcirc_tutorial_1.circ as structural Verilog: 1 circuit, main circuit main
module main (
  input  in_1,
  input  in_2,
  output out_3
);

  // NOT_Gate not_1 is placed but not wired
  // NOT_Gate not_2 is placed but not wired
  // AND_Gate and_1 is placed but not wired
  // AND_Gate and_2 is placed but not wired
  // OR_Gate or_1 is placed but not wired
endmodule
